# Fritzing sketch Tot_NANO (saved by Fritzing 0.9.3b)
breadboards: 1

parts:
  Part1 = Arduino Nano (Rev3.0)
  RHT1 = Humidity and Temperature Sensor RHT03
  Part2 = MicroSD Card Module
  Part3 = Barometric Pressure Sensor - BMP180 Breakout (GY-68)
  R1 = Resistor [tolerance=±5% resistance=220 package=THT]
  DS1 = DS18B20 1-Wire Temperature Sensor [part_number=DS18B20]

nets:
  GND: Part1.GND, RHT1.GND_1, Part2.GND, Part3.GND, DS1.GND
  N1: Part1.D2, R1.Pin_1, DS1.DQ
  N2: Part1.D4, Part2.CS
  N3: Part1.D8, RHT1.Data-signal
  N4: Part1.D11/MOSI, Part2.MOSI
  N5: Part1.D12/MISO, Part2.MISO
  VCC: Part1.5V, RHT1.Vcc, Part2.VCC, Part3.SCL, R1.Pin_0, DS1.VDD
  N6: Part1.A7, Part3.SDA
  3V3: Part1.3V3, Part3.VCC
  N7: Part1.D13/SCK, Part2.SCK
