# Fritzing sketch Untitled Sketch 6 (saved by Fritzing 0.9.3b)
breadboards: 1

parts:
  Part1 = Arduino Nano (Rev3.0)
  Part2 = Barometric Pressure Sensor - BMP180 Breakout (GY-68)

nets:
  GND: Part1.GND, Part1.D7, Part2.GND
  N1: Part1.D5, Part1.A4, Part2.SDA
  N2: Part1.D6, Part1.A5, Part2.SCL
  3V3: Part1.D8, Part1.3V3, Part2.VCC
