# Fritzing sketch dht11 (saved by Fritzing 0.9.3b)
breadboards: 1

parts:
  RHT1 = Humidity and Temperature Sensor RHT03
  Part1 = Arduino Nano (Rev3.0)

nets:
  VCC: RHT1.Vcc, Part1.5V
  N1: RHT1.Data-signal, Part1.D8
  N2: RHT1.GND_1, Part1.GND
