# Fritzing sketch ds18b20 (saved by Fritzing 0.9.3b)
breadboards: 1

parts:
  Part1 = Arduino Nano (Rev3.0)
  DS1 = DS18B20 1-Wire Temperature Sensor [part_number=DS18B20]
  R1 = Resistor [tolerance=±5% resistance=220 package=THT]

nets:
  GND: Part1.GND, DS1.GND
  N1: Part1.D2, DS1.DQ, R1.Pin_0
  5V: Part1.5V, DS1.VDD, R1.Pin_1
