# Fritzing sketch fritzing ds18b20_definitiu (saved by Fritzing 0.9.2b)
breadboards: 1

parts:
  Part1 = Arduino Uno (Rev3)
  T1 = LM35 Temperature Sensor [package="TO92 [THT]"]
  Part2 = Barometric Pressure Sensor - BMP085 Breakout  # not connected
  R1 = Resistor [tolerance=±5% resistance=220 package="2512 [SMD]"]

nets:
  GND: Part1.GND, T1.GND
  N1: Part1.D2, T1.Vout, R1.Pin_1
  N2: Part1.5V, T1.+Vs, R1.Pin_0

notes:
  Resistor = 4k7 ohms
